# Fritzing sketch Rave Control V2_PCB (saved by Fritzing 0.9.9b)
circuit board: 7.83088cm x 3.34792cm
breadboards: 1

parts:
  1602_LCD = female pin header, 16 pins [form="♀ (female)"]
  470 = Resistor [tolerance=±5% power=0.25 resistance=220 package=THT]
  Loco_Electro_Rave_Control_V2 = Arduino Nano (Rev3.0)
  Contrast = female pin header, 3 pins [form="♀ (female)"]
  220 = Resistor [tolerance=±5% power=0.25 resistance=220 package=THT]
  4_7K = Resistor [tolerance=±5% power=0.25 resistance=220 package=THT]
  10n = Ceramic Capacitor [capacitance=100nF voltage=35V package="100 mil [THT, multilayer]"]
  12V = Camdenboss CTB0158-6 [part_number=CTB0158-6 package=THT]
  817 = Sharp PC817 [package=THT]
  100n = Ceramic Capacitor [capacitance=100nF voltage=35V package="100 mil [THT, multilayer]"]
  1K = Resistor [tolerance=±5% power=0.25 resistance=220 package=THT]
  1K_2 = Resistor [tolerance=±5% power=0.25 resistance=220 package=THT]
  4007 = Rectifier Diode [part_number=1N4001 package="300 mil [THT]"]
  470µF = Electrolytic Capacitor [capacitance=1µF voltage=35V package="200 mil [THT, electrolytic]"]
  4007_2 = Rectifier Diode [part_number=1N4001 package="300 mil [THT]"]
  15_3V_>| = female pin header, 1 pin [form="♀ (female)"]
  PWM = female pin header, 1 pin [form="♀ (female)"]
  5_7 = Zener Diode [part_number=1N4732A breakdown_voltage=3.6V package="300 mil [THT]"]
  Pic- = female pin header, 1 pin [form="♀ (female)"]
  Pic+ = female pin header, 1 pin [form="♀ (female)"]
  GND = female pin header, 1 pin [form="♀ (female)"]
  TX = female pin header, 1 pin [form="♀ (female)"]
  6_8V_>| = female pin header, 1 pin [form="♀ (female)"]
  RPM = female pin header, 2 pins [form="♀ (female)"]

nets:
  N1: 1602_LCD.pin1, 1602_LCD.pin5, 1602_LCD.pin16, Loco_Electro_Rave_Control_V2.GND, Contrast.pin3, 10n.0, 12V.pin5, 817.Pin_3, 470µF.-, PWM.pin1, 5_7.anode, Pic+.pin1, TX.pin1, 6_8V_>|.pin1
  N2: 1602_LCD.pin2, Loco_Electro_Rave_Control_V2.5V, Contrast.pin1, 4_7K.Pin_0, RPM.pin1
  N3: 1602_LCD.pin3, Contrast.pin2
  N4: 1602_LCD.pin4, Loco_Electro_Rave_Control_V2.D12/MISO
  N5: 1602_LCD.pin6, Loco_Electro_Rave_Control_V2.D11/MOSI
  N6: 1602_LCD.pin11, Loco_Electro_Rave_Control_V2.D6
  N7: 1602_LCD.pin12, Loco_Electro_Rave_Control_V2.D5
  N8: 1602_LCD.pin13, Loco_Electro_Rave_Control_V2.D4
  N9: 1602_LCD.pin14, Loco_Electro_Rave_Control_V2.D2
  N10: 1602_LCD.pin15, 470.Pin_0
  N11: 470.Pin_1, 12V.pin4, 4007_2.anode
  N12: Loco_Electro_Rave_Control_V2.D1/TX, 12V.pin6
  N13: Loco_Electro_Rave_Control_V2.D3, 4_7K.Pin_1, 10n.1, 817.Pin_4
  N14: Loco_Electro_Rave_Control_V2.D9, 220.Pin_0
  N15: Loco_Electro_Rave_Control_V2.VIN, 470µF.+, 4007_2.cathode, 15_3V_>|.pin1
  N16: Loco_Electro_Rave_Control_V2.A1, RPM.pin2
  N17: 220.Pin_1, 12V.pin1, 5_7.cathode, Pic-.pin1, GND.pin1
  N18: 12V.pin2, 1K_2.Pin_1
  N19: 12V.pin3, 1K.Pin_1
  N20: 817.Pin_1, 100n.1, 1K_2.Pin_0, 4007.cathode
  N21: 817.Pin_2, 100n.0, 1K.Pin_0, 4007.anode
